# Fritzing sketch driver (saved by Fritzing 0.8.0b)
breadboards: 1

parts:
  J1 = female pin header, 3 pins [form="♀ (female)"]
  J2 = female pin header, 2 pins [form="♀ (female)"]
  J3 = female pin header, 8 pins [form="♀ (female)"]
  J4 = female pin header, 3 pins [form="♀ (female)"]
  J5 = female pin header, 2 pins [form="♀ (female)"]
  TPIC6B1 = TPIC6B595 [chip_label=TPIC6B595 package="DIP (Dual Inline) [THT]"]

nets:
  N1: J1.pin1, TPIC6B1.SER_IN
  N2: J1.pin2, J4.pin2, TPIC6B1.SRCK
  N3: J1.pin3, J4.pin3, TPIC6B1.RCK
  N4: J2.pin1, J5.pin1, TPIC6B1.~G, TPIC6B1.GND
  N5: J2.pin2, J5.pin2, TPIC6B1.VCC, TPIC6B1.~SRCLR
  N6: J3.pin1, TPIC6B1.DRAIN0
  N7: J3.pin2, TPIC6B1.DRAIN1
  N8: J3.pin3, TPIC6B1.DRAIN2
  N9: J3.pin4, TPIC6B1.DRAIN3
  N10: J3.pin5, TPIC6B1.DRAIN4
  N11: J3.pin6, TPIC6B1.DRAIN5
  N12: J3.pin7, TPIC6B1.DRAIN6
  N13: J3.pin8, TPIC6B1.DRAIN7
  N14: J4.pin1, TPIC6B1.SER_OUT

notes:
  woozle.org/derby
  driver
  Build your own!

custom parts:
  TPIC6B595: Power Logic 8-bit Shift Register
